# Fritzing sketch Fading (saved by Fritzing 0.9.2b)
breadboards: 1

parts:
  LED1 = LED - 5mm [color="Red (633nm)" package="5 mm [THT]"]
  R2 = Resistor [tolerance=±5% resistance=220 package=THT]
  Parte1 = Arduino Uno (Rev3)

nets:
  N1: LED1.cathode, R2.Pin_0
  N2: LED1.anode, Parte1.D9_PWM
  N3: R2.Pin_1, Parte1.GND
